// Logisim project Logisim circuit diagram.circ as structural Verilog: 1 circuit, main circuit main
module main (
  input  Door_Sensor__D,
  input  Window_Sensor_W,
  input  Motion_Sensor_M,
  input  System_Armed_S,
  output Alaram_A
);

  wire or_1_out;

  or or_1 (or_1_out, Door_Sensor__D, Window_Sensor_W, Motion_Sensor_M);
  and and_1 (Alaram_A, or_1_out, System_Armed_S);

  // Notes on the sheet:
  //   Logic diagram
  //   A=S.(D+W+M)
endmodule
